# Fritzing sketch emg project (saved by Fritzing 0.9.3b)
circuit board: 8.46667cm x 5.64444cm
breadboards: 1

parts:
  Part1 = Arduino Uno (Rev3)
  M1 = advancer muscle sensor v3
  BAT2 = BC9VPC [package=bc9vpc]
  BAT1 = BC9VPC [package=bc9vpc]
  M2 = Dagu DGServo 9g (Top view) [part_number=RS001B]
  M3 = Dagu DGServo 9g (Top view) [part_number=RS001B]
  M4 = Dagu DGServo 9g (Top view) [part_number=RS001B]
  M5 = Dagu DGServo 9g (Top view) [part_number=RS001B]
  M6 = Dagu DGServo 9g (Top view) [part_number=RS001B]
  VCC1 = Battery

nets:
  N1: Part1.A0, M1.SIG
  N2: Part1.D9_PWM, M6.pulse
  N3: Part1.D10_PWM/SS, M2.pulse
  GND: Part1.GND, M1.GND, BAT2.V-, BAT1.V+, M2.gnd, M3.gnd, M4.gnd, M5.gnd, M6.gnd, VCC1.-
  N4: Part1.D3_PWM, M3.pulse
  N5: Part1.D5_PWM, M4.pulse
  N6: Part1.D6_PWM, M5.pulse
  VCC: Part1.VIN, M2.vcc, M3.vcc, M4.vcc, M5.vcc, M6.vcc, VCC1.+
  N7: M1.+Vs, BAT2.V+
  N8: M1.-Vs, BAT1.V-

custom parts:
  advancer muscle sensor v3: This sensor will measure the filtered and rectified electrical activity of a muscle; outputting 0-Vs Volts depending the amount of activity in the selected muscle, where Vs signifies the voltage of the power source. Power supply voltage: min. +-3.5V.
